// Digital circuit Lab02.dig as structural Verilog
module Lab02 (
  input  B,
  input  C,
  input  A,
  input  D,
  output Fa,
  output Fb,
  output Fc,
  output Fd,
  output Fe,
  output Fg,
  output Ff
);

  wire A_t, AB, AC, ADnB, ADnC, AnB, AnBnC, AnC, BC, BCnD, BDnA, BDnC, BnA, BnAnC, BnAnD, BnC, CDnA, CnA,
       CnAnB, CnB, CnD, DnA, DnC, nA, nAnB, nAnBnD, nAnC, nAnCnD, nB, nBnD, nC, nD;

  not not_1 (nB, A);
  not not_2 (nB, A);
  not not_3 (nC, C);
  not not_4 (nD, D);
  and and_1 (CnD, C, nD);
  and and_2 (CnB, C, nB);
  and and_3 (nAnC, nA, nC);
  and and_4 (nBnD, nB, nD);
  and and_5 (BC, C, A);
  and and_6 (AnC, A_t, nC);
  and and_7 (DnC, D, nC);
  and and_8 (CnA, C, nA);
  and and_9 (nAnB, nA, nB);
  and and_10 (BnA, nA, A);
  and and_11 (AnB, A_t, nB);
  and and_12 (DnA, nA, D);
  and and_13 (AC, C, A_t);
  and and_14 (BnC, A, nC);
  and and_15 (BDnA, nA, A, D);
  and and_16 (nAnCnD, nA, nC, nD);
  and and_17 (ADnC, A_t, nC, D);
  and and_18 (CDnA, nA, C, D);
  and and_19 (ADnB, A_t, nB, D);
  and and_20 (BDnC, nC, A, D);
  and and_21 (nAnBnD, nA, nB, nD);
  and and_22 (BCnD, C, A, nD);
  and and_23 (CnAnB, nA, nB, C);
  and and_24 (BnAnC, nA, A, nC);
  and and_25 (BnAnD, nA, A, nD);
  or or_1 (Fa, CnA, BC, nBnD, BDnA, AnBnC);
  or or_2 (Fb, nAnB, nBnD, nAnCnD, ADnC, CDnA);
  or or_3 (Fc, nAnC, BnA, DnC, AnB, DnA);
  or or_4 (Fd, AnC, ADnB, BDnC, nAnBnD, BCnD, CnAnB);
  or or_5 (Fe, CnD, AB, nBnD, AC);
  or or_6 (Ff, AC, AnB, BnAnC, BnAnD, nAnCnD);
  or or_7 (Fg, A_t, BnC, CnD, CnB);
  Seven_Seg seven_seg_1 (.a(Fa), .b(Fb), .c(Fc), .d(Fd), .e(Fe), .f(Ff), .g(Fg), .dp(1'b0));

  assign B = A;
endmodule
